# Fritzing sketch led-strip-wireless-controller (saved by Fritzing 0.9.3b)
breadboards: 1

parts:
  WeMos_D1_Mini1 = WeMos D1 Mini
  Part1 = Jtron 1 Channel Optoisolated Relay Module [package=relay]
  R1 = Resistor [tolerance=±5% resistance=2.2k package="0805 [SMD]"]
  M1 = RioRand LM2596
  J1 = Power Jack [package=power_jack_combo]
  J2 = Power Jack [package=power_jack_combo]

nets:
  5V: WeMos_D1_Mini1.5V, Part1.VCC, M1.Pin_3
  N1: WeMos_D1_Mini1.D6, R1.Pin_0
  N2: WeMos_D1_Mini1.G, Part1.GND, M1.Pin_4
  N3: Part1.NO, J1.GNDBREAK
  N4: Part1.MAIN, M1.Pin_1, J2.GND
  N5: Part1.IN1, R1.Pin_1
  N6: M1.Pin_2, J1.GND, J2.GNDBREAK
